# Fritzing sketch MOSQUITO REPPLENT USING 555 TIMER (saved by Fritzing 0.9.6b)
circuit board: 6.94863cm x 5.22213cm
breadboards: 1

parts:
  IC1 = General purpose bipolar Timer [package=dil-08]
  LED1 = LED - 3mm [color="Red (633nm)" current=0.030 package="3 mm [THT]"]
  R1 = Resistor [tolerance=±5% power=0.25 resistance=220 package=THT]
  C1 = Capacitor [package=cap-pth-large]
  U1 = POT [package=pot_alpha_rv16af-20]
  SPKR1 = Loudspeaker
  C2 = Capacitor [package=cap-pth-large]
  R2 = Resistor [tolerance=±5% power=0.25 resistance=220 package=THT]
  S1 = Momentary Switch [package=tactile-pth]
  VCC1 = Battery block 9V

nets:
  N1: IC1.GND, SPKR1.pin2
  N2: IC1.TRI, IC1.TRE, U1.S
  N3: IC1.OUT, SPKR1.pin1
  N4: IC1._RES, IC1.VCC+, R1.Pin_1, R2.Pin_1, S1.3
  N5: IC1.CON, C2.1
  N6: IC1.DIS, R1.Pin_0, U1.A
  GND: LED1.cathode, C1.2, C2.2, VCC1.-
  N7: LED1.anode, R2.Pin_0
  N8: C1.1, U1.E
  N9: S1.2, VCC1.+
